// Logisim project DF_lab1_task4.circ as structural Verilog: 1 circuit, main circuit main
module main (
  input  A,
  input  B,
  input  C
);

  wire A_prime_B_prime_out, A_prime_C_prime_out, AB_prime_C_prime_out, ABC_out, not_1_out, not_2_out,
       not_3_out, or_1_out, or_2_out;

  not not_1 (not_1_out, B);
  not not_2 (not_2_out, A);
  not not_3 (not_3_out, C);
  and A_prime_C_prime (A_prime_C_prime_out, not_2_out, not_3_out);
  and A_prime_B_prime (A_prime_B_prime_out, not_2_out, not_1_out);
  and AB_prime_C_prime (AB_prime_C_prime_out, A, not_1_out, not_3_out);
  and ABC (ABC_out, A, B, C);
  or or_1 (or_1_out, A_prime_C_prime_out, A_prime_B_prime_out, AB_prime_C_prime_out);
  or or_2 (or_2_out, A_prime_C_prime_out, A_prime_B_prime_out, ABC_out);

  // Notes on the sheet:
  //   F1
  //   F2
endmodule
