// Logisim project DF_lab1.circ as structural Verilog: 1 circuit, main circuit main
module main (
  input  A,
  input  B,
  input  [2:0] in_3
);

  wire and_1_out, and_2_out, and_3_out, and_4_out, decoder_1_out0, decoder_1_out1, decoder_1_out2,
       decoder_1_out3, decoder_1_out4, decoder_1_out5, decoder_1_out6, decoder_1_out7, not_1_out, not_2_out,
       or_1_out, or_2_out, or_3_out, or_4_out, or_5_out;

  not not_1 (not_1_out, A);
  not not_2 (not_2_out, B);
  and and_1 (and_1_out, A, B);
  and and_2 (and_2_out, A, not_2_out);
  and and_3 (and_3_out, not_1_out, B);
  and and_4 (and_4_out, not_1_out, not_2_out);
  or or_1 (or_1_out, and_2_out, and_3_out);
  or or_2 (or_2_out, and_1_out, and_4_out);
  LED led_1 (.in(or_1_out));
  LED led_2 (.in(or_2_out));
  Decoder #(.select(3), .enable("false")) decoder_1 (
    .out0(decoder_1_out0), .out1(decoder_1_out1), .out2(decoder_1_out2), .out3(decoder_1_out3),
    .out4(decoder_1_out4), .out5(decoder_1_out5), .out6(decoder_1_out6), .out7(decoder_1_out7), .sel(in_3));
  or or_3 (or_3_out, decoder_1_out5, decoder_1_out4, decoder_1_out7, decoder_1_out3);
  or or_4 (or_4_out, decoder_1_out0, decoder_1_out2, decoder_1_out5, decoder_1_out6);
  or or_5 (or_5_out, decoder_1_out0, decoder_1_out1, decoder_1_out2, decoder_1_out5, decoder_1_out7);

  // Notes on the sheet:
  //   AB
  //   AB'
  //   A'B
  //   A'B'
  //   F1(A'B+AB')
  //   F2(AB+A'B')
  //   A'B'C'
  //   A'B'C
  //   A'BC'
  //   A'BC
  //   AB'C'
  //   AB'C
  //   ABC'
  //   ABC
  //   F1
  //   F2
  //   F3
endmodule
