// Logisim project DF_lab1_task3.circ as structural Verilog: 1 circuit, main circuit main
module main (
  input  A,
  input  B,
  input  C,
  input  D,
  input  _0_input
);

  wire and_1_out, and_2_out, and_3_out, and_4_out, and_5_out, and_6_out, and_7_out, and_8_out, and_9_out,
       and_10_out, and_11_out, and_12_out, not_1_out, not_2_out, not_3_out, not_4_out, not_5_out, not_6_out,
       or_1_out, or_2_out, or_3_out, or_4_out;

  not not_1 (not_1_out, A);
  not not_2 (not_2_out, B);
  not not_3 (not_3_out, C);
  not not_4 (not_4_out, D);
  not not_5 (not_5_out, or_1_out);
  and and_1 (and_1_out, not_1_out, not_2_out, C, not_4_out);
  and and_2 (and_2_out, A, B, not_3_out, not_4_out);
  and and_3 (and_3_out, A, B, not_3_out, D);
  buf and_4 (and_4_out, A);  // AND_Gate
  buf and_5 (and_5_out, _0_input);  // AND_Gate
  and and_6 (and_6_out, B, C, D);
  and and_7 (and_7_out, not_2_out, not_3_out, D);
  and and_8 (and_8_out, A, B, not_3_out);
  and and_9 (and_9_out, A, B, not_4_out);
  buf and_10 (and_10_out, or_1_out);  // AND_Gate
  and and_11 (and_11_out, not_1_out, not_2_out, not_3_out, D);
  and and_12 (and_12_out, A, not_2_out, not_3_out, not_4_out);
  or or_1 (or_1_out, and_1_out, and_2_out, and_3_out);
  or or_2 (or_2_out, and_4_out, and_5_out, and_6_out);
  or or_3 (or_3_out, and_7_out, and_8_out, and_9_out);
  or or_4 (or_4_out, and_10_out, and_11_out, and_12_out);
  not not_6 (not_6_out, or_3_out);

  // Notes on the sheet:
  //   F1
  //   F2
  //   F3
  //   F4
endmodule
